// Logisim project gate-intro.circ as structural Verilog: 1 circuit, main circuit main
module main (
  input  x,
  input  y,
  output x_prime,
  output out_4,
  output xy,
  output x_y,
  output xy__prime,
  output x_y__prime,
  output x_XOR_y,
  output x_NOR
);

  Clock clock_1 ();  // open: out
  not \not  (x_prime, x);
  buf buffer (out_4, x);
  and \and  (xy, x, y);
  or \or  (x_y, x, y);
  nand Nand (xy__prime, x, y);
  nor Nor (x_y__prime, x, y);
  xor xor_1 (x_XOR_y, x, y);
  xnor xnor_1 (x_NOR, x, y);

  // Notes on the sheet:
  //   This is a not gate
endmodule
