// Logisim project lab2p1.circ as structural Verilog: 1 circuit, main circuit main
module main (
  input  b,
  input  a,
  input  cin,
  output out_4,
  output sum
);

  wire not_1_out;

  not not_1 (not_1_out, b);
  Multiplexer #(.select(2), .enable("false")) multiplexer_1 (
    .in0(a), .in1(b), .in2(b), .in3(a), .out(out_4), .sel({cin, a}));
  Multiplexer #(.select(2), .enable("false")) multiplexer_2 (
    .in0(b), .in1(not_1_out), .in2(not_1_out), .in3(b), .out(sum), .sel({cin, a}));
endmodule
