// Logisim project lab2p2.circ as structural Verilog: 1 circuit, main circuit main
module main (
  input  in_1
);

  wire clock_1_out;
  wire [1:0] rom_1_data;
  wire [2:1] register_1_q;

  ROM #(.addrWidth(3), .dataWidth(2)) rom_1 (.addr({register_1_q, in_1}), .data(rom_1_data));  // open: sel
  Clock clock_1 (.out(clock_1_out));
  Register #(.width(2)) register_1 (.D(rom_1_data), .Q(register_1_q), .clk(clock_1_out));  // open: en, clr
  Hex_Digit_Display hex_digit_display_1 (.value({2'b00, register_1_q}));  // open: dp

  // Notes on the sheet:
  //   contents of rom_1 (hex, n*v repeats v):
  //   1 3 0 2 3 1 2
endmodule
