// Logisim project lab2p3.circ as structural Verilog: 1 circuit, main circuit main
module main (
  input  in_1,
  input  in_2
);

  wire clock_1_out;
  wire [2:0] register_1_q, rom_1_data;

  ROM #(.addrWidth(5), .dataWidth(3)) rom_1 (.addr({register_1_q, in_2, in_1}), .data(rom_1_data));  // open: sel
  Clock clock_1 (.out(clock_1_out));
  Register #(.width(3)) register_1 (.D(rom_1_data), .Q(register_1_q), .clk(clock_1_out));  // open: en, clr
  Hex_Digit_Display hex_digit_display_1 (.value({1'b0, register_1_q}));  // open: dp

  // Notes on the sheet:
  //   contents of rom_1 (hex, n*v repeats v):
  //   1 2 5 6 2 3 6 6 3 4 6 6 4 5 6 6 5 7*6 1 2 5 6
endmodule
