// Logisim project majority.circ as structural Verilog: 1 circuit, main circuit main
module main (
  input  z,
  input  y,
  input  x,
  input  x_2,
  input  y_2,
  input  z_2,
  output out_7,
  output out_8
);

  wire not_1_out, not_2_out, not_3_out, x_prime_out, x_prime_y_z_out, x_y_prime_z_out, x_y_z_out,
       x_y_z_prime_out, z_y_out;

  not x_prime (x_prime_out, x);
  not not_1 (not_1_out, x_2);
  not not_2 (not_2_out, x_2);
  not not_3 (not_3_out, z_2);
  and z_y (z_y_out, z, y);
  or or_1 (out_7, z_y_out, x_prime_out);
  and x_prime_y_z (x_prime_y_z_out, not_1_out, x_2, z_2);
  and x_y_prime_z (x_y_prime_z_out, x_2, not_2_out, z_2);
  and x_y_z_prime (x_y_z_prime_out, x_2, x_2, not_3_out);
  and x_y_z (x_y_z_out, x_2, x_2, z_2);
  or or_2 (out_8, x_prime_y_z_out, x_y_prime_z_out, x_y_z_prime_out, x_y_z_out);

  assign y_2 = x_2;
endmodule
